// Logisim project Cache.circ as structural Verilog: 8 circuits, main circuit parse_address
module implementation (
  input  [9:0] CpuAddressIn,
  input  CpuReadIn,
  input  CpuWriteIn,
  input  [7:0] CpuWriteValueIn,
  input  [31:0] LineFromMemIn,
  input  ClkIn,
  output ReadyOut,
  output DidContainOut,
  output [7:0] ByteReadOut,
  output [7:0] MemAddressOut,
  output MemReadOut,
  output MemWriteOut,
  output [31:0] Line2MemOut
);

  wire and_1_out, and_2_out, cpu_set, CpuRead, CpuWrite, feedRead, feedWrite, initializing, instruc_enable,
       not_1_out, set0_dirty, set0_hit, set1_dirty, set1_hit, updateAges, washit, waydirty;
  wire [1:0] offset;
  wire [2:0] current_state, nextstatelogic_1_next_state;
  wire [6:0] cpu_tag;
  wire [7:0] CpuWriteValue, set0_byteRead, set0_maddress, set1_byteRead, set1_maddress;
  wire [9:0] CpuAddress;
  wire [31:0] set0_Line2Mem, set1_Line2Mem;

  and and_1 (and_1_out, ReadyOut, CpuReadIn);
  and and_2 (and_2_out, ReadyOut, CpuWriteIn);
  or or_1 (instruc_enable, and_1_out, and_2_out);
  Register #(.width(10)) register_1 (.D(CpuAddressIn), .en(instruc_enable), .clk(ClkIn), .Q(CpuAddress));  // open: clr
  Register #(.width(1)) register_2 (.D(CpuReadIn), .en(instruc_enable), .clk(ClkIn), .Q(CpuRead));  // open: clr
  Register #(.width(1)) register_3 (.D(CpuWriteIn), .en(instruc_enable), .clk(ClkIn), .Q(CpuWrite));  // open: clr
  Register register_4 (.D(CpuWriteValueIn), .en(instruc_enable), .clk(ClkIn), .Q(CpuWriteValue));  // open: clr
  Multiplexer #(.enable("false")) multiplexer_1 (.in0(CpuRead), .in1(CpuReadIn), .out(feedRead), .sel(instruc_enable));
  Multiplexer #(.enable("false")) multiplexer_2 (
    .in0(CpuWrite), .in1(CpuWriteIn), .out(feedWrite), .sel(instruc_enable));
  not not_1 (not_1_out, cpu_set);
  parse_address parse_address_1 (.in_1(CpuAddress), .out_2(offset), .out_3(cpu_set), .out_4(cpu_tag));
  set set0 (
    .clk(ClkIn), .write_in(CpuWrite), .linefromMem(LineFromMemIn), .CpuWriteValueIn(CpuWriteValue),
    .CpuAddress_in(CpuAddress), .init(initializing), .memRead(CpuRead), .updateAgesin(updateAges),
    .usingThisSet(not_1_out), .contains(set0_hit), .dirty(set0_dirty), .byteReadOut(set0_byteRead),
    .lineToMem(set0_Line2Mem), .address_out(set0_maddress));
  set set1 (
    .clk(ClkIn), .write_in(CpuWrite), .linefromMem(LineFromMemIn), .CpuWriteValueIn(CpuWriteValue),
    .CpuAddress_in(CpuAddress), .init(initializing), .memRead(CpuRead), .updateAgesin(updateAges),
    .usingThisSet(cpu_set), .contains(set1_hit), .dirty(set1_dirty), .byteReadOut(set1_byteRead),
    .lineToMem(set1_Line2Mem), .address_out(set1_maddress));
  nextstatelogic nextstatelogic_1 (
    .state(current_state), .read(CpuRead), .write(CpuWrite), .dirty(waydirty), .hit(washit),
    .next_state(nextstatelogic_1_next_state));
  Register #(.width(3)) register_5 (
    .D(nextstatelogic_1_next_state), .en(1'b1), .clk(ClkIn), .Q(current_state));  // open: clr
  // Probe on current_state
  Multiplexer #(.enable("false")) multiplexer_3 (.in0(set0_hit), .in1(set1_hit), .out(washit), .sel(cpu_set));
  Multiplexer #(.enable("false"), .width(8)) multiplexer_4 (
    .in0(set0_byteRead), .in1(set1_byteRead), .out(ByteReadOut), .sel(cpu_set));
  Multiplexer #(.enable("false")) multiplexer_5 (.in0(set0_dirty), .in1(set1_dirty), .out(waydirty), .sel(cpu_set));
  Multiplexer #(.enable("false"), .width(32)) multiplexer_6 (
    .in0(set0_Line2Mem), .in1(set1_Line2Mem), .out(Line2MemOut), .sel(cpu_set));
  Multiplexer #(.enable("false"), .width(8)) multiplexer_7 (
    .in0(set0_maddress), .in1(set1_maddress), .out(MemAddressOut), .sel(cpu_set));
  output_logic output_logic_1 (
    .current_state(current_state), .read(CpuRead), .write(CpuWrite), .tagdirty(waydirty), .was_hit(washit),
    .ReadyOut(ReadyOut), .DidContainOut(DidContainOut), .MemReadOut(MemReadOut), .MemWriteOut(MemWriteOut),
    .updateAges(updateAges), .initializing(initializing));

  // Other names for the same wires on the sheet: clk = ClkIn; CpuAddress_in[9:0] = CpuAddressIn;
  //   CpuRead_in = CpuReadIn; CpuWrite_in = CpuWriteIn; CpuWriteValue_in[7:0] = CpuWriteValueIn;
  //   DidContain = DidContainOut; LineFromMem[31:0] = LineFromMemIn; MemAddress[7:0] = MemAddressOut;
  //   MemRead = MemReadOut; MemWrite = MemWriteOut; Ready = ReadyOut; ByteRead[7:0] = ByteReadOut;
  //   SelectedSetByteRead[7:0] = ByteReadOut; Line2Mem[31:0] = Line2MemOut; SelectedSetLine2Mem[31:0] = Line2MemOut

  // Notes on the sheet:
  //   registers for all CPU info
  //   enable on Ready AND read or AND write
  //   this will correc the bytes
  //   always send saved ones to the set
  //   used saved CPU details when any state except ready
endmodule

module parse_address (
  input  [9:0] in_1,
  output [1:0] out_2,
  output out_3,
  output [6:0] out_4
);


  assign out_2 = in_1[1:0];
  assign out_3 = in_1[2];
  assign out_4 = in_1[9:3];

  // Other names for the same wires on the sheet: CpuAddress[9:0] = in_1; Offset[1:0] = in_1[1:0]; Set = in_1[2];
  //   Tag[6:0] = in_1[9:3]
endmodule

module way (
  input  clock,
  input  [1:0] Age_in,
  input  [31:0] fromMem_in,
  input  [7:0] writeNew_in,
  input  write_in,
  input  usingthisway,
  input  [9:0] CpuAddress_in,
  input  memRead_in,
  input  updateAges,
  output hit,
  output [7:0] byteReadOut,
  output dirty,
  output [1:0] age,
  output [31:0] sendToMem,
  output [7:0] address_out
);

  wire and_2_out, and_3_out, and_4_out, and_5_out, and_6_out, and_7_out, and_8_out, comparator_1_eq, d_in,
       FSM_write0, FSM_write1, FSM_write2, FSM_write3, not_1_out, or_1_out, or_2_out, or_3_out, or_4_out,
       or_5_out, valid_out;
  wire [1:0] offset;
  wire [6:0] tag_out;
  wire [7:0] multiplexer_1_out, multiplexer_2_out, multiplexer_3_out, multiplexer_4_out;

  parse_address parse_address_1 (
    .in_1(CpuAddress_in), .out_2(offset), .out_3(address_out[0]), .out_4(address_out[7:1]));
  not not_1 (not_1_out, hit);
  and and_1 (d_in, usingthisway, write_in);
  Demultiplexer #(.select(2)) demultiplexer_1 (
    .out0(FSM_write0), .out1(FSM_write1), .out2(FSM_write2), .out3(FSM_write3), .in(write_in), .sel(offset),
    .en(not_1_out));
  Multiplexer #(.enable("false"), .width(8)) multiplexer_1 (
    .in0(fromMem_in[7:0]), .in1(writeNew_in), .out(multiplexer_1_out), .sel(FSM_write0));
  Multiplexer #(.enable("false"), .width(8)) multiplexer_2 (
    .in0(fromMem_in[15:8]), .in1(writeNew_in), .out(multiplexer_2_out), .sel(FSM_write1));
  Multiplexer #(.enable("false"), .width(8)) multiplexer_3 (
    .in0(fromMem_in[23:16]), .in1(writeNew_in), .out(multiplexer_3_out), .sel(FSM_write2));
  Multiplexer #(.enable("false"), .width(8)) multiplexer_4 (
    .in0(fromMem_in[31:24]), .in1(writeNew_in), .out(multiplexer_4_out), .sel(FSM_write3));
  or or_1 (or_1_out, memRead_in, FSM_write0);
  or or_2 (or_2_out, memRead_in, FSM_write1);
  or or_3 (or_3_out, memRead_in, FSM_write2);
  or or_4 (or_4_out, memRead_in, FSM_write3);
  and and_2 (and_2_out, or_1_out, usingthisway);
  and and_3 (and_3_out, or_2_out, usingthisway);
  and and_4 (and_4_out, or_3_out, usingthisway);
  and and_5 (and_5_out, or_4_out, usingthisway);
  Register byte0_reg (.D(multiplexer_1_out), .en(and_2_out), .clk(clock), .Q(sendToMem[7:0]));  // open: clr
  Register byte1_reg (.D(multiplexer_2_out), .en(and_3_out), .clk(clock), .Q(sendToMem[15:8]));  // open: clr
  Register byte2_reg (.D(multiplexer_3_out), .en(and_4_out), .clk(clock), .Q(sendToMem[23:16]));  // open: clr
  Register byte3_reg (.D(multiplexer_4_out), .en(and_5_out), .clk(clock), .Q(sendToMem[31:24]));  // open: clr
  or or_5 (or_5_out, memRead_in, write_in);
  and and_6 (and_6_out, or_5_out, usingthisway);
  and and_7 (and_7_out, memRead_in, usingthisway);
  and and_8 (and_8_out, memRead_in, usingthisway);
  Multiplexer #(.select(2), .width(8)) multiplexer_5 (
    .in0(sendToMem[7:0]), .in1(sendToMem[15:8]), .in2(sendToMem[23:16]), .in3(sendToMem[31:24]),
    .out(byteReadOut), .sel(offset), .en(memRead_in));
  // Probe on byteReadOut
  Register #(.width(1)) dirty_reg (.D(d_in), .en(and_6_out), .clk(clock), .Q(dirty));  // open: clr
  Register #(.width(1)) valid_reg (.D(memRead_in), .en(and_7_out), .clk(clock), .Q(valid_out));  // open: clr
  Register #(.width(2)) age_reg (.D(Age_in), .en(updateAges), .clk(clock), .Q(age));  // open: clr
  Register #(.width(7)) tag_reg (.D(address_out[7:1]), .en(and_8_out), .clk(clock), .Q(tag_out));  // open: clr
  Comparator #(.mode("unsigned"), .width(7)) comparator_1 (
    .a(address_out[7:1]), .b(tag_out), .eq(comparator_1_eq));  // open: gt, lt
  and and_9 (hit, comparator_1_eq, usingthisway, valid_out);

  // Other names for the same wires on the sheet: a_in[1:0] = Age_in; cpu_set = address_out[0];
  //   cpu_tag[6:0] = address_out[7:1]; age_out[1:0] = age; byteOut[7:0] = byteReadOut; clk = clock; contains = hit;
  //   CpuAddress[9:0] = CpuAddress_in; cpuwrite_val[7:0] = writeNew_in; dirty_out = dirty;
  //   b0_mem[7:0] = fromMem_in[7:0]; b1_mem[7:0] = fromMem_in[15:8]; b2_mem[7:0] = fromMem_in[23:16];
  //   b3_mem[7:0] = fromMem_in[31:24]; memread = memRead_in; b0[7:0] = sendToMem[7:0]; output_block[31:0] = sendToMem;
  //   b1[7:0] = sendToMem[15:8]; b2[7:0] = sendToMem[23:16]; b3[7:0] = sendToMem[31:24]; selected = usingthisway;
  //   updateAge = updateAges; write = write_in

  // Notes on the sheet:
  //   dirty is one anytime we are selected and write
  //   Read the byte in this way at the given offset
  //   Did this way have a hit?
endmodule

module set (
  input  clk,
  input  write_in,
  input  [31:0] linefromMem,
  input  [7:0] CpuWriteValueIn,
  input  [9:0] CpuAddress_in,
  input  init,
  input  memRead,
  input  updateAgesin,
  input  usingThisSet,
  output contains,
  output dirty,
  output [7:0] byteReadOut,
  output [31:0] lineToMem,
  output [7:0] address_out
);

  wire and_1_out, and_2_out, and_3_out, and_7_out, and_8_out, and_9_out, and_10_out, and_11_out, and_12_out,
       cpu_set, dirty_w0, dirty_w1, dirty_w2, h0, h1, h2, not_1_out, not_2_out, offset_dirty, old0, old1,
       old2, or_1_out, or_2_out, or_3_out, useWay0, useWay1, useWay2, wantToWrite, writeBack_dirty;
  wire [1:0] age_w0, age_w0_new, age_w1, age_w1_new, age_w2, age_w2_new, hitIndex, offset_in, oldestWayIndex;
  wire [6:0] cpu_tag;
  wire [7:0] byte0, byte1, byte2, memReadOut_w0, memReadOut_w1, memReadOut_w2;
  wire [31:0] sendMem_w0, sendMem_w1, sendMem_w2;

  parse_address parse_address_1 (.in_1(CpuAddress_in), .out_2(offset_in), .out_3(cpu_set), .out_4(cpu_tag));
  and and_1 (and_1_out, write_in, usingThisSet);
  and and_2 (and_2_out, memRead, usingThisSet);
  and and_3 (and_3_out, updateAgesin, usingThisSet);
  // Probe on hitIndex
  BitFinder #(.width(3)) bitfinder_1 (.in({h2, h1, h0}), .index(hitIndex), .found(contains));
  // Probe on oldestWayIndex
  not not_1 (not_1_out, contains);
  Demultiplexer #(.enable("false"), .select(2)) demultiplexer_1 (
    .out0(old0), .out1(old1), .out2(old2), .in(not_1_out), .sel(oldestWayIndex));  // open: out3
  way way0 (
    .clock(clk), .Age_in(age_w0_new), .fromMem_in(linefromMem), .writeNew_in(CpuWriteValueIn),
    .write_in(and_1_out), .usingthisway(useWay0), .CpuAddress_in(CpuAddress_in), .memRead_in(and_2_out),
    .updateAges(and_3_out), .hit(h0), .byteReadOut(byte0), .dirty(dirty_w0), .age(age_w0),
    .sendToMem(sendMem_w0), .address_out(memReadOut_w0));
  oldest_way_selector oldest_way_selector_1 (
    .way0_age(age_w0), .way1_age(age_w1), .way2_age(age_w2), .oldestway(oldestWayIndex));
  and and_4 (useWay0, usingThisSet, or_1_out);
  or or_1 (or_1_out, h0, old0);
  and and_5 (useWay1, usingThisSet, or_2_out);
  or or_2 (or_2_out, h1, old1);
  and and_6 (useWay2, usingThisSet, or_3_out);
  or or_3 (or_3_out, h2, old2);
  and and_7 (and_7_out, write_in, usingThisSet);
  and and_8 (and_8_out, memRead, usingThisSet);
  and and_9 (and_9_out, updateAgesin, usingThisSet);
  way way1 (
    .clock(clk), .Age_in(age_w1_new), .fromMem_in(linefromMem), .writeNew_in(CpuWriteValueIn),
    .write_in(and_7_out), .usingthisway(useWay1), .CpuAddress_in(CpuAddress_in), .memRead_in(and_8_out),
    .updateAges(and_9_out), .hit(h1), .byteReadOut(byte1), .dirty(dirty_w1), .age(age_w1),
    .sendToMem(sendMem_w1), .address_out(memReadOut_w1));
  updateages updateages_1 (
    .hitIndex(hitIndex), .init(init), .age0_in(age_w0), .age1_in(age_w1), .age2_in(age_w2),
    .updateAgesIn(updateAgesin), .w0_age(age_w0_new), .w1_age(age_w1_new), .w2_age(age_w2_new));
  and and_10 (and_10_out, write_in, usingThisSet);
  and and_11 (and_11_out, updateAgesin, usingThisSet);
  and and_12 (and_12_out, memRead, usingThisSet);
  Multiplexer #(.enable("false"), .select(2)) multiplexer_1 (
    .in0(dirty_w0), .in1(dirty_w1), .in2(dirty_w2), .out(writeBack_dirty), .sel(oldestWayIndex));  // open: in3
  Multiplexer #(.enable("false"), .select(2)) multiplexer_2 (
    .in0(dirty_w0), .in1(dirty_w1), .in2(dirty_w2), .out(offset_dirty), .sel(offset_in));  // open: in3
  Multiplexer #(.enable("false"), .select(2), .width(32)) multiplexer_3 (
    .in0(sendMem_w0), .in1(sendMem_w1), .in2(sendMem_w2), .out(lineToMem), .sel(oldestWayIndex));  // open: in3
  not not_2 (not_2_out, writeBack_dirty);
  // Probe on lineToMem
  way way2 (
    .clock(clk), .Age_in(age_w2_new), .fromMem_in(linefromMem), .writeNew_in(CpuWriteValueIn),
    .write_in(and_10_out), .usingthisway(useWay2), .CpuAddress_in(CpuAddress_in), .memRead_in(and_12_out),
    .updateAges(and_11_out), .hit(h2), .byteReadOut(byte2), .dirty(dirty_w2), .age(age_w2),
    .sendToMem(sendMem_w2), .address_out(memReadOut_w2));
  nand nand_1 (wantToWrite, contains, 1'b0, not_2_out);
  Multiplexer #(.enable("false")) multiplexer_4 (
    .in0(offset_dirty), .in1(writeBack_dirty), .out(dirty), .sel(wantToWrite));
  Multiplexer #(.enable("false"), .select(2), .width(8)) multiplexer_5 (
    .in0(byte0), .in1(byte1), .in2(byte2), .out(byteReadOut), .sel(hitIndex));  // open: in3
  Multiplexer #(.enable("false"), .select(2), .width(8)) multiplexer_6 (
    .in0(memReadOut_w0), .in1(memReadOut_w1), .in2(memReadOut_w2), .out(address_out), .sel(hitIndex));  // open: in3

  // Other names for the same wires on the sheet: clock = clk; CpuAddress[9:0] = CpuAddress_in; dirty_out = dirty;
  //   fromMem[31:0] = linefromMem; hit = contains; initializing = init; memreadIN = memRead;
  //   newValue[7:0] = CpuWriteValueIn; updateAge = updateAgesin; usingSet = usingThisSet; write = write_in;
  //   writeBack[31:0] = lineToMem

  // Notes on the sheet:
  //   If wanttowrite, return the dirty of the highest age index
  //   If do not wanttowrite, return the dirty of way determined by offset
  //   IF hit fail & highestAge dirty, we want to write to memory
  //   IF hit succeds, don't write to memory
endmodule

module output_logic (
  input  [2:0] current_state,
  input  read,
  input  write,
  input  tagdirty,
  input  was_hit,
  output ReadyOut,
  output DidContainOut,
  output MemReadOut,
  output MemWriteOut,
  output updateAges,
  output initializing
);

  wire and_1_out, and_2_out, and_3_out, and_4_out, and_5_out, and_6_out, and_7_out, and_8_out, and_9_out,
       and_10_out, and_11_out, and_12_out, and_13_out, and_14_out, and_15_out, and_16_out, and_17_out,
       and_18_out, and_19_out, and_20_out, and_21_out, and_22_out, not_1_out, not_2_out, not_3_out,
       not_4_out, not_5_out;

  not not_1 (not_1_out, current_state[2]);
  not not_2 (not_2_out, current_state[1]);
  not not_3 (not_3_out, current_state[0]);
  not not_4 (not_4_out, read);
  not not_5 (not_5_out, write);
  and and_1 (and_1_out, not_1_out, not_2_out, not_3_out, read, write);
  and and_2 (and_2_out, not_1_out, not_2_out, current_state[0], not_4_out);
  and and_3 (and_3_out, not_2_out, current_state[0], not_5_out);
  and and_4 (and_4_out, current_state[0], read, not_5_out);
  and and_5 (and_5_out, current_state[1], current_state[0], write);
  and and_6 (and_6_out, current_state[2], not_4_out, not_5_out);
  and and_7 (and_7_out, current_state[2], current_state[1], not_5_out);
  and and_8 (and_8_out, current_state[0], was_hit);
  and and_9 (and_9_out, current_state[1], was_hit);
  and and_10 (and_10_out, current_state[2], was_hit);
  and and_11 (and_11_out, read, write);
  and and_12 (and_12_out, current_state[1], not_3_out);
  and and_13 (and_13_out, current_state[1], write);
  and and_14 (and_14_out, current_state[2], current_state[1]);
  and and_15 (and_15_out, not_2_out, read, write, tagdirty);
  and and_16 (and_16_out, current_state[2], not_2_out, not_3_out, not_4_out);
  and and_17 (and_17_out, current_state[2], not_2_out, not_3_out, not_5_out);
  and and_18 (and_18_out, not_1_out, not_2_out, not_3_out);
  and and_19 (and_19_out, not_2_out, not_3_out, not_4_out, write);
  and and_20 (and_20_out, not_2_out, not_3_out, read, not_5_out);
  and and_21 (and_21_out, current_state[1], current_state[0], not_4_out, write);
  and and_22 (and_22_out, current_state[2], current_state[0]);
  and and_23 (initializing, not_1_out, not_2_out, not_3_out);
  or or_1 (ReadyOut, and_1_out, and_2_out, and_3_out, and_4_out, and_5_out, and_6_out, and_7_out);
  or or_2 (DidContainOut, and_8_out, and_9_out, and_10_out);
  or or_3 (MemReadOut, and_11_out, and_12_out, and_13_out, and_14_out);
  or or_4 (MemWriteOut, and_15_out, and_16_out, and_17_out);
  or or_5 (updateAges, and_18_out, and_19_out, and_20_out, and_21_out, and_22_out);
endmodule

module nextstatelogic (
  input  [2:0] state,
  input  read,
  input  write,
  input  dirty,
  input  hit,
  output [2:0] next_state
);

  wire and_1_out, and_2_out, and_3_out, and_4_out, and_5_out, and_6_out, and_7_out, and_8_out, not_1_out,
       not_2_out, not_3_out, not_4_out, not_5_out, not_6_out, not_7_out;

  not not_1 (not_1_out, state[2]);
  not not_2 (not_2_out, state[1]);
  not not_3 (not_3_out, state[0]);
  not not_4 (not_4_out, read);
  not not_5 (not_5_out, write);
  not not_6 (not_6_out, dirty);
  not not_7 (not_7_out, hit);
  and and_1 (and_1_out, not_2_out, state[0], write, dirty);
  and and_2 (and_2_out, state[0], read, dirty);
  and and_3 (and_3_out, not_2_out, state[0], write, not_6_out);
  and and_4 (and_4_out, state[0], read, not_6_out, not_7_out);
  and and_5 (and_5_out, state[1], not_3_out, not_4_out);
  and and_6 (and_6_out, not_1_out, not_3_out);
  and and_7 (and_7_out, not_4_out, not_5_out);
  and and_8 (and_8_out, not_1_out, not_6_out, hit);
  or or_1 (next_state[2], and_1_out, and_2_out);
  or or_2 (next_state[1], and_3_out, and_4_out, and_5_out, state[2]);
  or or_3 (next_state[0], and_6_out, and_7_out, and_8_out, state[1]);
endmodule

module updateages (
  input  [1:0] hitIndex,
  input  init,
  input  [1:0] age0_in,
  input  [1:0] age1_in,
  input  [1:0] age2_in,
  input  updateAgesIn,
  output [1:0] w0_age,
  output [1:0] w1_age,
  output [1:0] w2_age
);

  wire and_1_out;
  wire [1:0] adder_1_out, adder_2_out, adder_3_out, age_w0_n, age_w1_n, age_w2_n, multiplexer_1_out;
  wire [2:0] a0_select, a1_select, a2_select;

  Multiplexer #(.enable("false"), .select(2), .width(2)) multiplexer_1 (
    .in0(age0_in), .in1(age1_in), .in2(age2_in), .out(multiplexer_1_out), .sel(hitIndex));  // open: in3
  Comparator #(.mode("unsigned"), .width(2)) comparator_1 (
    .a(age0_in), .b(multiplexer_1_out), .gt(a0_select[2]), .eq(a0_select[1]), .lt(a0_select[0]));
  Comparator #(.mode("unsigned"), .width(2)) comparator_2 (
    .a(age1_in), .b(multiplexer_1_out), .gt(a1_select[0]), .eq(a1_select[1]), .lt(a1_select[2]));
  Comparator #(.mode("unsigned"), .width(2)) comparator_3 (
    .a(age2_in), .b(multiplexer_1_out), .gt(a2_select[0]), .eq(a2_select[1]), .lt(a2_select[2]));
  Adder #(.width(2)) adder_1 (.a(age0_in), .b(2'b01), .out(adder_1_out));  // open: cin, cout
  Adder #(.width(2)) adder_2 (.a(age1_in), .b(2'b01), .out(adder_2_out));  // open: cin, cout
  Adder #(.width(2)) adder_3 (.a(age2_in), .b(2'b01), .out(adder_3_out));  // open: cin, cout
  Multiplexer #(.enable("false"), .select(3), .width(2)) multiplexer_2 (
    .in1(adder_1_out), .in2(2'b00), .in4(age0_in), .out(age_w0_n), .sel(a0_select));  // open: in0, in3, in5, in6, in7
  Multiplexer #(.enable("false"), .select(3), .width(2)) multiplexer_3 (
    .in1(adder_2_out), .in2(2'b00), .in4(age1_in), .out(age_w1_n), .sel(a1_select));  // open: in0, in3, in5, in6, in7
  Multiplexer #(.enable("false"), .select(3), .width(2)) multiplexer_4 (
    .in1(adder_3_out), .in2(2'b00), .in4(age2_in), .out(age_w2_n), .sel(a2_select));  // open: in0, in3, in5, in6, in7
  and and_1 (and_1_out, updateAgesIn, init);
  Multiplexer #(.enable("false"), .width(2)) multiplexer_5 (.in0(age_w0_n), .in1(2'b00), .out(w0_age), .sel(and_1_out));
  Multiplexer #(.enable("false"), .width(2)) multiplexer_6 (.in0(age_w1_n), .in1(2'b01), .out(w1_age), .sel(and_1_out));
  Multiplexer #(.enable("false"), .width(2)) multiplexer_7 (.in0(age_w2_n), .in1(2'b10), .out(w2_age), .sel(and_1_out));

  // Other names for the same wires on the sheet: age_w0[1:0] = age0_in; age_w1[1:0] = age1_in; age_w2[1:0] = age2_in;
  //   initializing = init; upAges = updateAgesIn

  // Notes on the sheet:
  //   If hit succeeds, MUX passes age of way accessed
  //   If hit fails, MUX passes age of w0
  //   If age > w accessed select = 100
  //   If age < w accessed select = 001
  //   If age = w accessed select = 010
endmodule

module oldest_way_selector (
  input  [1:0] way0_age,
  input  [1:0] way1_age,
  input  [1:0] way2_age,
  output [1:0] oldestway
);

  wire not_1_out, not_2_out;

  not not_1 (not_1_out, way0_age[1]);
  not not_2 (not_2_out, way1_age[1]);
  and and_1 (oldestway[1], not_1_out, not_2_out);

  assign oldestway[0] = way1_age[1];
endmodule
