// Logisim project bcd.circ as structural Verilog: 1 circuit, main circuit implementation
module implementation (
  input  w3,
  input  w2,
  input  w1,
  input  w0,
  output a,
  output b,
  output c,
  output d,
  output e,
  output f,
  output g
);

  wire AB_out, ABnC_out, AC_out, An, AnB_out, AnBn_out, AnC_out, AnCn_out, BCn_out, Bn, BnC_out, Cn, Dn;

  and ABnC (ABnC_out, w0, Bn, w2);
  and AB (AB_out, w0, w1);
  and AC (AC_out, w0, w2);
  and AnBn (AnBn_out, An, Bn);
  and AnCn (AnCn_out, An, Cn);
  and AnB (AnB_out, An, w1);
  and AnC (AnC_out, An, w2);
  and BCn (BCn_out, w1, Cn);
  and BnC (BnC_out, Bn, w2);
  not not_1 (Dn, w3);
  not not_2 (Cn, w2);
  not not_3 (Bn, w1);
  not not_4 (An, w0);
  or or_1 (a, w3, w1, AC_out, AnCn_out);
  or or_2 (b, Cn, AB_out, AnBn_out);
  or or_3 (c, w0, Bn, w2);
  or or_4 (d, w3, ABnC_out, AnB_out, AnCn_out, BCn_out);
  or or_5 (e, AnB_out, AnCn_out);
  or or_6 (f, AnBn_out, AnC_out, BnC_out, w3);
  or or_7 (g, w3, AnB_out, BCn_out, BnC_out);

  // Other names for the same wires on the sheet: at = a; bt = b; ct = c; dt = d; et = e; ft = f; gt = g; w0t = w0;
  //   w1t = w1; w2t = w2; w3t = w3
endmodule
