// Logisim project adder4.circ as structural Verilog: 1 circuit, main circuit implementation
module implementation (
  input  [3:0] Ain,
  input  [3:0] Bin,
  input  Cinin,
  output [3:0] Sum_Out,
  output Carry_Out
);

  wire A0B0_out, A1B1_out, A2B2_out, A3B3_out, carry0_out, carry1_out, carry2_out, G0_out, G1_out, G2_out,
       G3_out, P0_out, P0Cin_out, P1_out, P1G0_out, P1P0Cin_out, P2_out, P2G1_out, P2P1G0_out, P2P1P0Cin_out,
       P3_out, P3G2_out, P3P2G1_out, P3P2P1G0_out, P3P2P1P0Cin_out;

  and G0 (G0_out, Bin[0], Ain[0]);
  and G1 (G1_out, Bin[1], Ain[1]);
  and G2 (G2_out, Bin[2], Ain[2]);
  and G3 (G3_out, Bin[3], Ain[3]);
  xor P0 (P0_out, Bin[0], Ain[0]);
  xor P1 (P1_out, Bin[1], Ain[1]);
  xor P2 (P2_out, Bin[2], Ain[2]);
  xor P3 (P3_out, Bin[3], Ain[3]);
  xor A3B3 (A3B3_out, Ain[3], Bin[3]);
  xor A2B2 (A2B2_out, Ain[2], Bin[2]);
  xor A1B1 (A1B1_out, Ain[1], Bin[1]);
  xor A0B0 (A0B0_out, Ain[0], Bin[0]);
  and P3P2P1P0Cin (P3P2P1P0Cin_out, P3_out, P2_out, P1_out, P0_out, Cinin);
  and P3P2P1G0 (P3P2P1G0_out, P3_out, P2_out, P1_out, G0_out);
  and P3P2G1 (P3P2G1_out, P3_out, P2_out, G1_out);
  and P3G2 (P3G2_out, P3_out, G2_out);
  and P2P1P0Cin (P2P1P0Cin_out, P2_out, P1_out, P0_out, Cinin);
  and P2P1G0 (P2P1G0_out, P2_out, P1_out, G0_out);
  and P2G1 (P2G1_out, P2_out, G1_out);
  and P1P0Cin (P1P0Cin_out, P1_out, P0_out, Cinin);
  and P1G0 (P1G0_out, P1_out, G0_out);
  and P0Cin (P0Cin_out, P0_out, Cinin);
  ExactlyOne carry3 (
    .out(Carry_Out), .in0(P3P2P1P0Cin_out), .in1(P3P2P1G0_out), .in2(P3P2G1_out), .in3(P3G2_out), .in4(G3_out));
  ExactlyOne carry2 (.out(carry2_out), .in0(P2P1P0Cin_out), .in1(P2P1G0_out), .in2(P2G1_out), .in3(G2_out));
  ExactlyOne carry1 (.out(carry1_out), .in0(P1P0Cin_out), .in1(P1G0_out), .in2(G1_out));
  xor carry0 (carry0_out, P0Cin_out, G0_out);
  xor Sum3 (Sum_Out[3], A3B3_out, carry2_out);
  xor Sum2 (Sum_Out[2], A2B2_out, carry1_out);
  xor Sum1 (Sum_Out[1], A1B1_out, carry0_out);
  xor Sum0 (Sum_Out[0], A0B0_out, Cinin);

  // Other names for the same wires on the sheet: A[3:0] = Ain; B[3:0] = Bin; C3 = Carry_Out; Cin = Cinin;
  //   Sum[3:0] = Sum_Out
endmodule
