// Logisim project bitcounter.circ as structural Verilog: 1 circuit, main circuit implementation
module implementation (
  input  [7:0] BitsIn,
  input  CountZerosIn,
  output [3:0] BitCountOut
);

  wire not_2_out;
  wire [1:0] adder_1_out, adder_2_out, adder_3_out, adder_4_out, adder_5_out, adder_6_out, adder_7_out,
       adder_8_out, adder_9_out, adder_10_out, adder_11_out, adder_12_out;
  wire [2:0] adder_13_out, adder_14_out;
  wire [2:2] adder_9_cout, adder_10_cout, adder_11_cout, adder_12_cout;
  wire [3:3] adder_13_cout, adder_14_cout;
  wire [7:0] not_1_out;

  assign not_1_out = ~BitsIn;  // NOT_Gate not_1, 8 bits wide
  Adder #(.width(1)) adder_1 (.a(BitsIn[0]), .b(BitsIn[1]), .out(adder_1_out[0]), .cout(adder_1_out[1]));  // open: cin
  Adder #(.width(1)) adder_2 (.a(BitsIn[2]), .b(BitsIn[3]), .out(adder_2_out[0]), .cout(adder_2_out[1]));  // open: cin
  Adder #(.width(1)) adder_3 (.a(BitsIn[4]), .b(BitsIn[5]), .out(adder_3_out[0]), .cout(adder_3_out[1]));  // open: cin
  Adder #(.width(1)) adder_4 (.a(BitsIn[6]), .b(BitsIn[7]), .out(adder_4_out[0]), .cout(adder_4_out[1]));  // open: cin
  Adder #(.width(1)) adder_5 (
    .a(not_1_out[0]), .b(not_1_out[1]), .out(adder_5_out[0]), .cout(adder_5_out[1]));  // open: cin
  Adder #(.width(1)) adder_6 (
    .a(not_1_out[2]), .b(not_1_out[3]), .out(adder_6_out[0]), .cout(adder_6_out[1]));  // open: cin
  Adder #(.width(1)) adder_7 (
    .a(not_1_out[4]), .b(not_1_out[5]), .out(adder_7_out[0]), .cout(adder_7_out[1]));  // open: cin
  Adder #(.width(1)) adder_8 (
    .a(not_1_out[6]), .b(not_1_out[7]), .out(adder_8_out[0]), .cout(adder_8_out[1]));  // open: cin
  Adder #(.width(2)) adder_9 (
    .a(adder_1_out), .b(adder_2_out), .out(adder_9_out), .cout(adder_9_cout[2]));  // open: cin
  Adder #(.width(2)) adder_10 (
    .a(adder_3_out), .b(adder_4_out), .out(adder_10_out), .cout(adder_10_cout[2]));  // open: cin
  Adder #(.width(2)) adder_11 (
    .a(adder_5_out), .b(adder_6_out), .out(adder_11_out), .cout(adder_11_cout[2]));  // open: cin
  Adder #(.width(2)) adder_12 (
    .a(adder_7_out), .b(adder_8_out), .out(adder_12_out), .cout(adder_12_cout[2]));  // open: cin
  Adder #(.width(3)) adder_13 (
    .a({adder_9_cout[2], adder_9_out}), .b({adder_10_cout[2], adder_10_out}), .out(adder_13_out),
    .cout(adder_13_cout[3]));  // open: cin
  Adder #(.width(3)) adder_14 (
    .a({adder_11_cout[2], adder_11_out}), .b({adder_12_cout[2], adder_12_out}), .out(adder_14_out),
    .cout(adder_14_cout[3]));  // open: cin
  not not_2 (not_2_out, CountZerosIn);
  Multiplexer #(.enable("false"), .width(4)) multiplexer_1 (
    .in0({adder_14_cout[3], adder_14_out}), .in1({adder_13_cout[3], adder_13_out}), .out(BitCountOut),
    .sel(not_2_out));

  // Other names for the same wires on the sheet: BitCount[3:0] = BitCountOut; Bits[7:0] = BitsIn;
  //   CountZeros = CountZerosIn
endmodule
