// Logisim project shifter.circ as structural Verilog: 1 circuit, main circuit implementation
module implementation (
  input  IsRightShiftIn,
  input  IsArithmeticIn,
  input  [1:0] ShiftAmountIn,
  input  [2:0] NumberIn,
  output [2:0] ShiftedNumberOut
);

  wire decoder_1_out0, decoder_1_out1, decoder_2_out0, decoder_2_out1, decoder_3_out0, decoder_3_out1;

  Decoder #(.enable("false")) decoder_1 (.out0(decoder_1_out0), .out1(decoder_1_out1), .sel(IsArithmeticIn));
  Decoder decoder_2 (.out0(decoder_2_out0), .out1(decoder_2_out1), .sel(IsRightShiftIn), .en(decoder_1_out0));
  Decoder decoder_3 (.out0(decoder_3_out0), .out1(decoder_3_out1), .sel(IsRightShiftIn), .en(decoder_1_out1));
  Multiplexer #(.disabled("Z"), .select(2), .width(3)) multiplexer_1 (
    .in0(NumberIn), .in1({NumberIn[1:0], 1'b0}), .in2({NumberIn[0], 2'b00}), .in3(3'b000),
    .out(ShiftedNumberOut), .sel(ShiftAmountIn), .en(decoder_2_out0));
  Multiplexer #(.disabled("Z"), .select(2), .width(3)) multiplexer_2 (
    .in0(NumberIn), .in1({1'b0, NumberIn[2:1]}), .in2({2'b00, NumberIn[2]}), .in3(3'b000),
    .out(ShiftedNumberOut), .sel(ShiftAmountIn), .en(decoder_2_out1));
  Multiplexer #(.disabled("Z"), .select(2), .width(3)) multiplexer_3 (
    .in0(NumberIn), .in1({NumberIn[1:0], 1'b0}), .in2({NumberIn[0], 2'b00}), .in3(3'b000),
    .out(ShiftedNumberOut), .sel(ShiftAmountIn), .en(decoder_3_out0));
  Multiplexer #(.disabled("Z"), .select(2), .width(3)) multiplexer_4 (
    .in0(NumberIn), .in1({{2{NumberIn[2]}}, NumberIn[1]}), .in2({3{NumberIn[2]}}), .in3({3{NumberIn[2]}}),
    .out(ShiftedNumberOut), .sel(ShiftAmountIn), .en(decoder_3_out1));

  // Other names for the same wires on the sheet: ArithmeticOneLeft[2:1] = NumberIn[1:0];
  //   ArithmeticOneRight[2:0] = {{2{NumberIn[2]}}, NumberIn[1]}; LogicOneLeft[2:1] = NumberIn[1:0];
  //   LogicOneRight[1:0] = NumberIn[2:1]; Number[2:0] = NumberIn; ArithmeticThreeRight[2:0] = {3{NumberIn[2]}};
  //   ArithmeticTwoRight[2:0] = {3{NumberIn[2]}}; LogicTwoRight[0] = NumberIn[2]; ArithmeticTwoLeft[2] = NumberIn[0];
  //   LogicTwoLeft[2] = NumberIn[0]; IsArithmetic = IsArithmeticIn; IsRightShift = IsRightShiftIn;
  //   ShiftAmount[1:0] = ShiftAmountIn; ShiftedNumber[2:0] = ShiftedNumberOut
endmodule
