// Logisim project FourBitParity.circ as structural Verilog
module implementation (
  input  EnableIn,
  input  InputBitIn,
  input  ClkIn,
  output IsEvenOut
);

  wire [2:0] register_1_q, state_next_1_s0_next;

  state_next state_next_1 (
    .S2(register_1_q[2]), .S1(register_1_q[1]), .S0(register_1_q[0]), .InputBit(InputBitIn),
    .S2_Next(state_next_1_s0_next[2]), .S1_Next(state_next_1_s0_next[1]), .S0_Next(state_next_1_s0_next[0]));
  Register #(.width(3)) register_1 (
    .D(state_next_1_s0_next), .en(EnableIn), .clk(ClkIn), .Q(register_1_q));  // open: clr
  fsm_output fsm_output_1 (.S2(register_1_q[2]), .S1(register_1_q[1]), .S0(register_1_q[0]), .OutputBit(IsEvenOut));

  // Other names for the same wires on the sheet: Clk = ClkIn; Enable = EnableIn; InputBit = InputBitIn
endmodule

module state_next (
  input  S2,
  input  S1,
  input  S0,
  input  InputBit,
  output S2_Next,
  output S1_Next,
  output S0_Next
);

  wire and_1_out, and_2_out, and_3_out, and_4_out, and_5_out, and_6_out, and_7_out, and_8_out, and_9_out,
       and_10_out, and_11_out, and_12_out, not_1_out, not_2_out, not_3_out, not_4_out;

  not not_1 (not_1_out, S2);
  not not_2 (not_2_out, S1);
  not not_3 (not_3_out, S0);
  not not_4 (not_4_out, InputBit);
  and and_1 (and_1_out, not_1_out, S0, InputBit);
  and and_2 (and_2_out, S1, not_4_out);
  and and_3 (and_3_out, S2, not_3_out, InputBit);
  and and_4 (and_4_out, not_1_out, not_2_out, InputBit);
  and and_5 (and_5_out, not_1_out, not_2_out, S0);
  and and_6 (and_6_out, not_2_out, S0, InputBit);
  and and_7 (and_7_out, not_1_out, S1, not_4_out);
  and and_8 (and_8_out, S1, not_3_out, InputBit);
  and and_9 (and_9_out, not_1_out, not_2_out, not_4_out);
  and and_10 (and_10_out, S0, not_4_out);
  and and_11 (and_11_out, S1, not_3_out, InputBit);
  and and_12 (and_12_out, S2, not_3_out, InputBit);
  or or_1 (S2_Next, and_1_out, and_2_out, and_3_out);
  or or_2 (S1_Next, and_4_out, and_5_out, and_6_out, and_7_out, and_8_out);
  or or_3 (S0_Next, and_9_out, and_10_out, and_11_out, and_12_out);
endmodule

module fsm_output (
  input  S2,
  input  S1,
  input  S0,
  output OutputBit
);

  wire not_1_out;

  not not_1 (not_1_out, S1);
  and and_1 (OutputBit, S2, not_1_out, S0);
endmodule
