// Logisim project UpDownCounter.circ as structural Verilog: 2 circuits, main circuit implementation
module implementation (
  input  EnableIn,
  input  CountUpIn,
  input  CountDownIn,
  input  clkIn,
  output [2:0] Count
);

  wire [2:0] state_next_1_s0_next;

  state_next state_next_1 (
    .S2(Count[2]), .S1(Count[1]), .S0(Count[0]), .Up(CountUpIn), .Down(CountDownIn),
    .S2_Next(state_next_1_s0_next[2]), .S1_Next(state_next_1_s0_next[1]), .S0_Next(state_next_1_s0_next[0]));
  Register #(.width(3)) register_1 (.D(state_next_1_s0_next), .en(EnableIn), .clk(clkIn), .Q(Count));  // open: clr

  // Other names for the same wires on the sheet: clk = clkIn; CountDown = CountDownIn; CountUp = CountUpIn;
  //   Enable = EnableIn
endmodule

module state_next (
  input  S2,
  input  S1,
  input  S0,
  input  Up,
  input  Down,
  output S2_Next,
  output S1_Next,
  output S0_Next
);

  wire and_1_out, and_2_out, and_3_out, and_4_out, and_5_out, and_6_out, and_7_out, and_8_out, and_9_out,
       and_10_out, and_11_out, and_12_out, and_13_out, and_14_out, not_1_out, not_2_out, not_3_out, not_4_out;

  not not_1 (not_1_out, S1);
  not not_2 (not_2_out, S0);
  not not_3 (not_3_out, Up);
  not not_4 (not_4_out, Down);
  and and_1 (and_1_out, S1, S0, Up);
  and and_2 (and_2_out, S2, not_4_out);
  and and_3 (and_3_out, S2, S0);
  and and_4 (and_4_out, S2, S1);
  and and_5 (and_5_out, not_1_out, S0, Up);
  and and_6 (and_6_out, S1, not_2_out, not_4_out);
  and and_7 (and_7_out, S1, S0, not_3_out);
  and and_8 (and_8_out, S2, not_1_out, not_2_out, Down);
  and and_9 (and_9_out, S2, S1, not_4_out);
  and and_10 (and_10_out, not_2_out, Up);
  and and_11 (and_11_out, S0, not_3_out, not_4_out);
  and and_12 (and_12_out, S1, not_2_out, Down);
  and and_13 (and_13_out, S2, not_2_out, Down);
  and and_14 (and_14_out, S2, S1, S0, not_4_out);
  or or_1 (S2_Next, and_1_out, and_2_out, and_3_out, and_4_out);
  or or_2 (S1_Next, and_5_out, and_6_out, and_7_out, and_8_out, and_9_out);
  or or_3 (S0_Next, and_10_out, and_11_out, and_12_out, and_13_out, and_14_out);
endmodule
