// Logisim project Vending.circ as structural Verilog: 3 circuits, main circuit implementation
module implementation (
  input  EnableIn,
  input  QuarterReceivedIn,
  input  DimeReceivedIn,
  input  NickelReceivedIn,
  input  ClkIn,
  output Give_Mechandise_Out,
  output Give_Dime_Out,
  output Give_Nickel_Out
);

  wire [2:0] register_1_q, state_next_1_s0_next;

  state_next state_next_1 (
    .S2(register_1_q[2]), .S1(register_1_q[1]), .S0(register_1_q[0]), .I2(QuarterReceivedIn),
    .I1(DimeReceivedIn), .I0(NickelReceivedIn), .S2_Next(state_next_1_s0_next[2]),
    .S1_Next(state_next_1_s0_next[1]), .S0_Next(state_next_1_s0_next[0]));
  Register #(.width(3)) register_1 (
    .D(state_next_1_s0_next), .en(EnableIn), .clk(ClkIn), .Q(register_1_q));  // open: clr
  output_circ output_circ_1 (
    .S2(register_1_q[2]), .S1(register_1_q[1]), .S0(register_1_q[0]), .I2(QuarterReceivedIn),
    .I1(DimeReceivedIn), .I0(NickelReceivedIn), .Out_2(Give_Mechandise_Out), .Out_1(Give_Dime_Out),
    .Out_0(Give_Nickel_Out));

  // Other names for the same wires on the sheet: clk = ClkIn; Enable = EnableIn; Give_Dime = Give_Dime_Out;
  //   Give_Merchandise = Give_Mechandise_Out; Give_Nickel = Give_Nickel_Out;
  //   Inputs[2:0] = {QuarterReceivedIn, DimeReceivedIn, NickelReceivedIn}; NickelReceieved = NickelReceivedIn;
  //   DimeReceieved = DimeReceivedIn; QuarterReceieved = QuarterReceivedIn
endmodule

module state_next (
  input  S2,
  input  S1,
  input  S0,
  input  I2,
  input  I1,
  input  I0,
  output S2_Next,
  output S1_Next,
  output S0_Next
);

  wire and_1_out, and_2_out, and_3_out, and_4_out, and_5_out, and_6_out, and_7_out, and_8_out, and_9_out,
       and_10_out, and_11_out, and_12_out, and_13_out, and_14_out, not_1_out, not_2_out, not_3_out,
       not_4_out, not_5_out, not_6_out;

  not not_1 (not_1_out, S2);
  not not_2 (not_2_out, S1);
  not not_3 (not_3_out, S0);
  not not_4 (not_4_out, I2);
  not not_5 (not_5_out, I1);
  not not_6 (not_6_out, I0);
  and and_1 (and_1_out, not_2_out, not_3_out, I2);
  and and_2 (and_2_out, not_1_out, S1, I1);
  and and_3 (and_3_out, not_1_out, S1, S0, I0);
  and and_4 (and_4_out, S2, not_3_out, not_4_out, not_5_out);
  and and_5 (and_5_out, S2, not_4_out, not_5_out, not_6_out);
  and and_6 (and_6_out, not_1_out, I1);
  and and_7 (and_7_out, not_2_out, not_3_out, I2);
  and and_8 (and_8_out, not_1_out, S0, I0);
  and and_9 (and_9_out, S1, not_3_out, not_4_out, not_5_out);
  and and_10 (and_10_out, S1, not_4_out, not_5_out, not_6_out);
  and and_11 (and_11_out, not_3_out, I0);
  and and_12 (and_12_out, not_2_out, not_3_out, I2);
  and and_13 (and_13_out, not_1_out, S0, not_4_out, not_6_out);
  and and_14 (and_14_out, S0, not_4_out, not_5_out, not_6_out);
  or or_1 (S2_Next, and_1_out, and_2_out, and_3_out, and_4_out, and_5_out);
  or or_2 (S1_Next, and_6_out, and_7_out, and_8_out, and_9_out, and_10_out);
  or or_3 (S0_Next, and_11_out, and_12_out, and_13_out, and_14_out);
endmodule

module output_circ (
  input  S2,
  input  S1,
  input  S0,
  input  I2,
  input  I1,
  input  I0,
  output Out_2,
  output Out_1,
  output Out_0
);

  wire and_1_out, and_2_out, and_3_out, and_4_out, and_5_out, and_6_out, and_7_out, and_8_out, and_9_out,
       and_10_out, and_11_out, not_1_out;

  not not_1 (not_1_out, S0);
  and and_1 (and_1_out, S0, I2);
  and and_2 (and_2_out, S1, I2);
  and and_3 (and_3_out, S2, I1);
  and and_4 (and_4_out, S2, S0, I0);
  and and_5 (and_5_out, S1, S0, I2);
  and and_6 (and_6_out, S2, I2);
  and and_7 (and_7_out, S1, not_1_out, I2);
  and and_8 (and_8_out, S1, I2, I0);
  and and_9 (and_9_out, S1, I2, I1);
  and and_10 (and_10_out, S2, S0, I1);
  and and_11 (and_11_out, S2, S1, I2);
  or or_1 (Out_2, and_1_out, and_2_out, and_3_out, and_4_out);
  or or_2 (Out_1, and_5_out, and_6_out);
  or or_3 (Out_0, and_7_out, and_8_out, and_9_out, and_10_out, and_11_out);
endmodule
