// Logisim project CPU.circ as structural Verilog: 4 circuits, main circuit implementation
module implementation (
  input  [15:0] Instruction_In,
  input  ClkIn,
  output [4:0] Instruction_Address_Out,
  output [3:0] Reg0_Out,
  output [3:0] Reg1_Out,
  output [3:0] Reg2_Out,
  output [3:0] Reg3_Out,
  output [3:0] Reg4_Out,
  output [3:0] Reg5_Out,
  output [3:0] Reg6_Out,
  output [3:0] Reg7_Out,
  output [3:0] Reg8_Out,
  output [3:0] Reg9_Out,
  output [3:0] Reg10_Out,
  output [3:0] Reg11_Out,
  output [3:0] Reg12_Out,
  output [3:0] Reg13_Out,
  output [3:0] Reg14_Out,
  output [3:0] Reg15_Out
);

  wire letCount, letWrite, pickValue;
  wire [3:0] A_in, A_Value, B_in, B_Value, BorImm_in, C_in, Data_in, imm, multiplexer_1_out, opc;

  Counter #(.max('h1f), .width(5)) ProgramCounter (
    .count(letCount), .clk(ClkIn), .Q(Instruction_Address_Out));  // open: clr, load, up, D, carry
  instruction_decoder instruction_decoder_1 (
    .Instruction_In(Instruction_In), .A_in(A_in), .C_in(C_in), .BorImm_in(BorImm_in), .out_5(opc),
    .pickValue(pickValue));
  Demultiplexer #(.enable("false"), .width(4)) demultiplexer_1 (
    .out0(B_in), .out1(imm), .in(BorImm_in), .sel(pickValue));
  Multiplexer #(.enable("false"), .width(4)) multiplexer_1 (
    .in0(B_Value), .in1(imm), .out(multiplexer_1_out), .sel(pickValue));
  ALU alu_1 (
    .opCode(opc), .A_value(A_Value), .B_I_value(multiplexer_1_out), .enableCount(letCount),
    .enableWrite(letWrite), .ALU_out(Data_in));
  RegFile regfile_1 (
    .A_Sel_In(A_in), .B_Sel_In(B_in), .C_Sel_In(C_in), .Data_In(Data_in), .Reg_Write_In(letWrite),
    .clk_in(ClkIn), .A_Out(A_Value), .B_Out(B_Value), .Reg0_Out(Reg0_Out), .Reg1_Out(Reg1_Out),
    .Reg2_Out(Reg2_Out), .Reg3_Out(Reg3_Out), .Reg4_Out(Reg4_Out), .Reg5_Out(Reg5_Out), .Reg6_Out(Reg6_Out),
    .Reg7_Out(Reg7_Out), .Reg8_Out(Reg8_Out), .Reg9_Out(Reg9_Out), .Reg10_Out(Reg10_Out),
    .Reg11_Out(Reg11_Out), .Reg12_Out(Reg12_Out), .Reg13_Out(Reg13_Out), .Reg14_Out(Reg14_Out),
    .Reg15_Out(Reg15_Out));

  // Other names for the same wires on the sheet: Clk = ClkIn; Instruction[15:0] = Instruction_In;
  //   Instruction_Address[4:0] = Instruction_Address_Out; Reg0[3:0] = Reg0_Out; Reg1[3:0] = Reg1_Out;
  //   Reg2[3:0] = Reg2_Out; Reg3[3:0] = Reg3_Out; Reg4[3:0] = Reg4_Out; Reg5[3:0] = Reg5_Out; Reg6[3:0] = Reg6_Out;
  //   Reg7[3:0] = Reg7_Out; Reg8[3:0] = Reg8_Out; Reg9[3:0] = Reg9_Out; Reg10[3:0] = Reg10_Out;
  //   Reg11[3:0] = Reg11_Out; Reg12[3:0] = Reg12_Out; Reg13[3:0] = Reg13_Out; Reg14[3:0] = Reg14_Out;
  //   Reg15[3:0] = Reg15_Out

  // Notes on the sheet:
  //   Names: Nicole Pavlovich and Arianna-Rae Lagman
endmodule

module RegFile (
  input  [3:0] A_Sel_In,
  input  [3:0] B_Sel_In,
  input  [3:0] C_Sel_In,
  input  [3:0] Data_In,
  input  Reg_Write_In,
  input  clk_in,
  output [3:0] A_Out,
  output [3:0] B_Out,
  output [3:0] Reg0_Out,
  output [3:0] Reg1_Out,
  output [3:0] Reg2_Out,
  output [3:0] Reg3_Out,
  output [3:0] Reg4_Out,
  output [3:0] Reg5_Out,
  output [3:0] Reg6_Out,
  output [3:0] Reg7_Out,
  output [3:0] Reg8_Out,
  output [3:0] Reg9_Out,
  output [3:0] Reg10_Out,
  output [3:0] Reg11_Out,
  output [3:0] Reg12_Out,
  output [3:0] Reg13_Out,
  output [3:0] Reg14_Out,
  output [3:0] Reg15_Out
);

  wire Reg_Write0, Reg_Write1, Reg_Write2, Reg_Write3, Reg_Write4, Reg_Write5, Reg_Write6, Reg_Write7,
       Reg_Write8, Reg_Write9, Reg_Write10, Reg_Write11, Reg_Write12, Reg_Write13, Reg_Write14, Reg_Write15;

  Demultiplexer #(.enable("false"), .select(4)) demultiplexer_1 (
    .out0(Reg_Write0), .out1(Reg_Write1), .out2(Reg_Write2), .out3(Reg_Write3), .out4(Reg_Write4),
    .out5(Reg_Write5), .out6(Reg_Write6), .out7(Reg_Write7), .out8(Reg_Write8), .out9(Reg_Write9),
    .out10(Reg_Write10), .out11(Reg_Write11), .out12(Reg_Write12), .out13(Reg_Write13), .out14(Reg_Write14),
    .out15(Reg_Write15), .in(Reg_Write_In), .sel(C_Sel_In));
  Register #(.width(4)) register_1 (.D(Data_In), .en(Reg_Write0), .clk(clk_in), .Q(Reg0_Out));  // open: clr
  Register #(.width(4)) register_2 (.D(Data_In), .en(Reg_Write4), .clk(clk_in), .Q(Reg4_Out));  // open: clr
  Register #(.width(4)) register_3 (.D(Data_In), .en(Reg_Write8), .clk(clk_in), .Q(Reg8_Out));  // open: clr
  Register #(.width(4)) register_4 (.D(Data_In), .en(Reg_Write12), .clk(clk_in), .Q(Reg12_Out));  // open: clr
  Register #(.width(4)) register_5 (.D(Data_In), .en(Reg_Write1), .clk(clk_in), .Q(Reg1_Out));  // open: clr
  Register #(.width(4)) register_6 (.D(Data_In), .en(Reg_Write5), .clk(clk_in), .Q(Reg5_Out));  // open: clr
  Register #(.width(4)) register_7 (.D(Data_In), .en(Reg_Write9), .clk(clk_in), .Q(Reg9_Out));  // open: clr
  Register #(.width(4)) register_8 (.D(Data_In), .en(Reg_Write13), .clk(clk_in), .Q(Reg13_Out));  // open: clr
  Register #(.width(4)) register_9 (.D(Data_In), .en(Reg_Write2), .clk(clk_in), .Q(Reg2_Out));  // open: clr
  Register #(.width(4)) register_10 (.D(Data_In), .en(Reg_Write6), .clk(clk_in), .Q(Reg6_Out));  // open: clr
  Register #(.width(4)) register_11 (.D(Data_In), .en(Reg_Write10), .clk(clk_in), .Q(Reg10_Out));  // open: clr
  Register #(.width(4)) register_12 (.D(Data_In), .en(Reg_Write14), .clk(clk_in), .Q(Reg14_Out));  // open: clr
  Register #(.width(4)) register_13 (.D(Data_In), .en(Reg_Write3), .clk(clk_in), .Q(Reg3_Out));  // open: clr
  Register #(.width(4)) register_14 (.D(Data_In), .en(Reg_Write7), .clk(clk_in), .Q(Reg7_Out));  // open: clr
  Register #(.width(4)) register_15 (.D(Data_In), .en(Reg_Write11), .clk(clk_in), .Q(Reg11_Out));  // open: clr
  Register #(.width(4)) register_16 (.D(Data_In), .en(Reg_Write15), .clk(clk_in), .Q(Reg15_Out));  // open: clr
  Multiplexer #(.enable("false"), .select(4), .width(4)) multiplexer_1 (
    .in0(Reg0_Out), .in1(Reg1_Out), .in2(Reg2_Out), .in3(Reg3_Out), .in4(Reg4_Out), .in5(Reg5_Out),
    .in6(Reg6_Out), .in7(Reg7_Out), .in8(Reg8_Out), .in9(Reg9_Out), .in10(Reg10_Out), .in11(Reg11_Out),
    .in12(Reg12_Out), .in13(Reg13_Out), .in14(Reg14_Out), .in15(Reg15_Out), .out(A_Out), .sel(A_Sel_In));
  Multiplexer #(.enable("false"), .select(4), .width(4)) multiplexer_2 (
    .in0(Reg0_Out), .in1(Reg1_Out), .in2(Reg2_Out), .in3(Reg3_Out), .in4(Reg4_Out), .in5(Reg5_Out),
    .in6(Reg6_Out), .in7(Reg7_Out), .in8(Reg8_Out), .in9(Reg9_Out), .in10(Reg10_Out), .in11(Reg11_Out),
    .in12(Reg12_Out), .in13(Reg13_Out), .in14(Reg14_Out), .in15(Reg15_Out), .out(B_Out), .sel(B_Sel_In));

  // Other names for the same wires on the sheet: A[3:0] = A_Out; A_Sel[3:0] = A_Sel_In; B[3:0] = B_Out;
  //   B_Sel[3:0] = B_Sel_In; C_Sel[3:0] = C_Sel_In; clk = clk_in; Data[3:0] = Data_In; Reg0[3:0] = Reg0_Out;
  //   Reg1[3:0] = Reg1_Out; Reg2[3:0] = Reg2_Out; Reg3[3:0] = Reg3_Out; Reg4[3:0] = Reg4_Out; Reg5[3:0] = Reg5_Out;
  //   Reg6[3:0] = Reg6_Out; Reg7[3:0] = Reg7_Out; Reg8[3:0] = Reg8_Out; Reg9[3:0] = Reg9_Out; Reg10[3:0] = Reg10_Out;
  //   Reg11[3:0] = Reg11_Out; Reg12[3:0] = Reg12_Out; Reg13[3:0] = Reg13_Out; Reg14[3:0] = Reg14_Out;
  //   Reg15[3:0] = Reg15_Out; Reg_Write = Reg_Write_In
endmodule

module instruction_decoder (
  input  [15:0] Instruction_In,
  output [3:0] A_in,
  output [3:0] C_in,
  output [3:0] BorImm_in,
  output [3:0] out_5,
  output pickValue
);

  Multiplexer #(.enable("false"), .select(4)) multiplexer_1 (
    .in0(1'b0), .in1(1'b0), .in2(1'b1), .in3(1'b0), .in4(1'b0), .in5(1'b1), .in6(1'b0), .in7(1'b1),
    .in8(1'b0), .in9(1'b1), .in10(1'b0), .in11(1'b0), .in12(1'b0), .in13(1'b1), .in14(1'b0), .in15(1'b1),
    .out(pickValue), .sel(Instruction_In[15:12]));

  assign A_in = Instruction_In[7:4];
  assign BorImm_in = Instruction_In[3:0];
  assign C_in = Instruction_In[11:8];
  assign out_5 = Instruction_In[15:12];

  // Other names for the same wires on the sheet: B0_i1 = pickValue; BorImm[3:0] = Instruction_In[3:0];
  //   Instruction[15:0] = Instruction_In; A[3:0] = Instruction_In[7:4]; C[3:0] = Instruction_In[11:8];
  //   opcode[3:0] = Instruction_In[15:12]
endmodule

module ALU (
  input  [3:0] opCode,
  input  [3:0] A_value,
  input  [3:0] B_I_value,
  output enableCount,
  output enableWrite,
  output [3:0] ALU_out
);

  wire comparator_1_eq, comparator_2_eq, not_3_out;
  wire [3:0] ADDI_1101, ANDI_0101, NEGATE_1011, NOT_1010, ORI_0111, SUBI_1111, XORI_1001;

  assign ANDI_0101 = A_value & B_I_value;  // AND_Gate and_1, 4 bits wide
  assign ORI_0111 = A_value | B_I_value;  // OR_Gate or_1, 4 bits wide
  Comparator #(.width(4)) comparator_1 (.a(opCode), .b(4'b0000), .eq(comparator_1_eq));  // open: gt, lt
  Comparator #(.width(4)) comparator_2 (.a(opCode), .b(4'b0001), .eq(comparator_2_eq));  // open: gt, lt
  assign XORI_1001 = A_value ^ B_I_value;  // XOR_Gate xor_1, 4 bits wide
  assign NOT_1010 = ~A_value;  // NOT_Gate not_1, 4 bits wide
  Negator #(.width(4)) negator_1 (.in(A_value), .out(NEGATE_1011));
  Adder #(.width(4)) adder_1 (.a(A_value), .b(B_I_value), .out(ADDI_1101));  // open: cin, cout
  Subtractor #(.width(4)) subtractor_1 (.a(A_value), .b(B_I_value), .out(SUBI_1111));  // open: bin, bout
  not not_2 (enableCount, comparator_1_eq);
  not not_3 (not_3_out, comparator_2_eq);
  and and_2 (enableWrite, enableCount, not_3_out);
  Multiplexer #(.enable("false"), .select(4), .width(4)) multiplexer_1 (
    .in0(opCode), .in1(opCode), .in2(B_I_value), .in3(A_value), .in4(ANDI_0101), .in5(ANDI_0101),
    .in6(ORI_0111), .in7(ORI_0111), .in8(XORI_1001), .in9(XORI_1001), .in10(NOT_1010), .in11(NEGATE_1011),
    .in12(ADDI_1101), .in13(ADDI_1101), .in14(SUBI_1111), .in15(SUBI_1111), .out(ALU_out), .sel(opCode));

  // Other names for the same wires on the sheet: ADDR_1100[3:0] = ADDI_1101; ALUout[3:0] = ALU_out;
  //   ANDR_0100[3:0] = ANDI_0101; BI[3:0] = B_I_value; LOAD_0010[3:0] = B_I_value; A[3:0] = A_value;
  //   MOVE_0011[3:0] = A_value; NOP_0001[3:0] = opCode; op[3:0] = opCode; STOP_0000[3:0] = opCode;
  //   ORR_0110[3:0] = ORI_0111; SUBR_1110[3:0] = SUBI_1111; XORR_1000[3:0] = XORI_1001

  // Notes on the sheet:
  //   0000 STOP [cpu ceases execution]
  //   0001 NOP [do nothing]
  //   0010 LOAD [regC = immediate]
  //   0011 MOVE [regC = regA]
  //   0100 ANDR [regC = A * B
  //   0101 ANDI [regC = A*immediate]
  //   0110 ORR [regC = A + B
  //   0111 ORRI [regC = A + imm
  //   1000 XORR c = A xor B
  //   1001 XORI c = A xor imme
  //   1010 NOT [C = not A]
  //   1011 NEGATE [C = -A]
  //   1100 ADDR [C = A plus B]
  //   1101 ADDI [C = A plus imm]
  //   1110 SUBR [C=A minus B]
  //   1111 SUBI [C = A minus imm]
endmodule
